# Fritzing sketch L03_04_AnalogInput (saved by Fritzing 1.0.4)
breadboards: 1

parts:
  A1 = Particle - Photon2
  R6 = Trimmer Potentiometer [maximum_resistance=10kΩ knob_status=50% power=0.5W package=THT]

nets:
  N1: A1.Pin_2, R6.leg2
  N2: A1.Pin_4, R6.leg1
  N3: A1.Pin_5, R6.wiper

custom parts:
  Particle - Photon2: The Photon 2 is a microcontroller and Wi-Fi networking developed by particle. Features: 802.11a/b/g/n Wi-Fi, 2.4 GHz and 5 GHz Integrated PCB antenna Integrated U.FL connector for external antenna Integrated RF switch BLE 5 using same antenna as Wi-Fi Realtek RTL8721DM MCU ARM Cortex M33 CPU, 200 MHz 2048 KB (2 MB) user application maximum size 3072 KB (3 MB) of RAM available to user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
